// Logisim project KP8B.circ as structural Verilog: 5 circuits, main circuit main
module main (
  input  in_1
);

  wire and_1_out, and_2_out, and_3_out, and_4_out, and_5_out, and_6_out, and_7_out, and_8_out, and_9_out,
       and_10_out, and_11_out, and_12_out, and_13_out, and_14_out, and_16_out, and_17_out, C0, C1, C2, C3,
       C4, C5, C6, C7, CLK, clock_1_out, dipswitch_2_p1, dipswitch_2_p2, Enable, IRQ, keyboard_1_avail,
       KEYREAD, not_1_out, not_2_out, not_3_out, not_4_out, not_6_out, res, sH, sL, TERMINAL, WE;
  wire [3:0] multiplexer_2_out;
  wire [4:0] pla_2_out;
  wire [6:0] KEY;
  wire [7:0] Bin, C6_q, C7_q, DATA, Dh, Dl, multiplexer_1_out, ram_1_dout, rom_1_data, rom_2_data,
       ScreenIn_q, ScreenPos;
  wire [7:7] undriven;
  wire [15:0] kp8b_1_addr;
  wire [23:0] X_q;

  and and_1 (and_1_out, sL, WE);
  and and_2 (and_2_out, sH, WE);
  and and_3 (and_3_out, C0, WE);
  and and_4 (and_4_out, C1, WE);
  and and_5 (and_5_out, C2, WE);
  and and_6 (and_6_out, C3, WE);
  and and_7 (and_7_out, C4, WE);
  and and_8 (and_8_out, C6, WE);
  and and_9 (and_9_out, C7, WE);
  Register Cl (.D(DATA), .en(and_1_out), .clk(CLK), .Q(Dl));  // open: clr
  Register Ch (.D(DATA), .en(and_2_out), .clk(CLK), .Q(Dh));  // open: clr
  Register u_ScreenPos (.D(DATA), .en(and_3_out), .clk(CLK), .Q(ScreenPos));  // open: clr
  Register ScreenIn (.D(DATA), .en(and_4_out), .clk(CLK), .Q(ScreenIn_q));  // open: clr
  Register X (.D(DATA), .en(and_5_out), .clk(CLK), .Q(X_q[7:0]));  // open: clr
  Register Y (.D(DATA), .en(and_6_out), .clk(CLK), .Q(X_q[15:8]));  // open: clr
  Register Z (.D(DATA), .en(and_7_out), .clk(CLK), .Q(X_q[23:16]));  // open: clr
  Register u_C6 (.D(DATA), .en(and_8_out), .clk(CLK), .Q(C6_q));  // open: clr
  Register u_C7 (.D(DATA), .en(and_9_out), .clk(CLK), .Q(C7_q));  // open: clr
  Clock clock_1 (.out(clock_1_out));
  Multiplexer #(.select(4), .width(8)) multiplexer_1 (
    .in0(rom_2_data), .in1(ram_1_dout), .in2({8{1'b0}}), .in3({undriven[7], KEY}), .in4(Dl), .in5(Dh),
    .in6(Bin), .in7(ScreenPos), .in8(ScreenIn_q), .in9(X_q[7:0]), .in10(X_q[15:8]), .in11(X_q[23:16]),
    .in12(rom_1_data), .in13(C6_q), .in14(C7_q), .out(multiplexer_1_out), .sel(multiplexer_2_out));  // open: in15
  Multiplexer #(.width(4)) multiplexer_2 (
    .in0({3'b000, WE}), .in1(pla_2_out[3:0]), .out(multiplexer_2_out), .sel(pla_2_out[4]));
  PLA #(.in_width(4), .out_width(12), .\table ("0101 000000000001 # Sh\n0100 000000000010 # Sl\n0010 000000000100 # Terminal\n0011 000000001000 # Keyread\n0111 000000010000 # Matrix0\n1000 000000100000 # Matrix1\n1001 000001000000 # Matrix2\n1010 000010000000 # Matrix3\n1011 000100000000 # Matrix4\n1100 001000000000 # Matrix5\n1101 010000000000 # Matrix6\n1110 100000000000 # Matrix7")) pla_1 (
    .in(multiplexer_2_out), .out({C7, C6, C5, C4, C3, C2, C1, C0, KEYREAD, TERMINAL, sL, sH}));
  KP8B kp8b_1 (
    .DIN(multiplexer_1_out), .IRQ(IRQ), .NMI(in_1), .RES(res), .RDY(Enable), .CLK(clock_1_out),
    .ADDR(kp8b_1_addr), .R_W(WE), .CLKO(CLK), .DOUT(DATA));
  PLA #(.in_width(16), .out_width(5), .\table ("1111111111111110 10010 # TERMINAL\n1111111111111111 10011 # KEYBOARD\n1111111111111100 10100 # HEX-LOW\n1111111111111101 10101 # HEX-HIGH\n1111111111111011 10110 # Binary In\n1111111111110011 10111 # C0\n1111111111110100 11000 # C1\n1111111111110101 11001 # C2\n1111111111110110 11010 # C3\n1111111111110111 11011 # C4\n1111111111111000 11100 # C5\n1111111111111001 11101 # C6\n1111111111111010 11110 # C7")) pla_2 (
    .in(kp8b_1_addr), .out(pla_2_out));
  not not_1 (not_1_out, pla_2_out[4]);
  and and_10 (and_10_out, C5, WE);
  ROM #(.addrWidth(24)) rom_1 (.addr(X_q), .data(rom_1_data));
  ROM #(.addrWidth(15)) rom_2 (.addr(kp8b_1_addr[14:0]), .data(rom_2_data));
  RAM #(.addrWidth(15), .enables("line")) ram_1 (
    .addr(kp8b_1_addr[14:0]), .we(and_11_out), .clk(CLK), .din(DATA), .dout(ram_1_dout));
  and and_11 (and_11_out, kp8b_1_addr[15], WE, not_1_out);
  and and_12 (and_12_out, TERMINAL, WE);
  Hex_Digit_Display #(.decimalPoint("false")) hex_digit_display_1 (.value(Dh[7:4]));
  TTY tty_1 (.data(DATA[6:0]), .clk(CLK), .we(and_12_out), .clr(res));
  Keyboard #(.buflen(1)) keyboard_1 (.clk(CLK), .re(and_13_out), .clr(res), .avail(keyboard_1_avail), .data(KEY));
  and and_13 (and_13_out, KEYREAD, ~WE);  // AND_Gate
  Hex_Digit_Display #(.decimalPoint("false")) hex_digit_display_2 (.value(Dh[3:0]));
  Hex_Digit_Display #(.decimalPoint("false")) hex_digit_display_3 (.value(Dl[7:4]));
  and and_14 (and_14_out, keyboard_1_avail, dipswitch_2_p1);
  Hex_Digit_Display #(.decimalPoint("false")) hex_digit_display_4 (.value(Dl[3:0]));
  not not_2 (not_2_out, and_14_out);
  not not_3 (not_3_out, not_2_out);
  not not_4 (not_4_out, not_3_out);
  Button R (.out(res));
  and and_15 (IRQ, and_14_out, not_4_out);
  LedBar ledbar_1 (
    .led0(Dh[7]), .led1(Dh[6]), .led2(Dh[5]), .led3(Dh[4]), .led4(Dh[3]), .led5(Dh[2]), .led6(Dh[1]),
    .led7(Dh[0]));
  DipSwitch dipswitch_1 (
    .sw1(Bin[7]), .sw2(Bin[6]), .sw3(Bin[5]), .sw4(Bin[4]), .sw5(Bin[3]), .sw6(Bin[2]), .sw7(Bin[1]),
    .sw8(Bin[0]));
  // DipSwitch #(.number(2)) dipswitch_2: pin names not known; wires that end beside it: dipswitch_2_p1, dipswitch_2_p2
  LedBar ledbar_2 (
    .led0(Dl[7]), .led1(Dl[6]), .led2(Dl[5]), .led3(Dl[4]), .led4(Dl[3]), .led5(Dl[2]), .led6(Dl[1]),
    .led7(Dl[0]));
  not not_5 (Enable, dipswitch_2_p2);
  not not_6 (not_6_out, WE);
  and and_16 (and_16_out, not_6_out, C1);
  and and_17 (and_17_out, C1, WE);
  // RGB_Video #(.cursor("No Cursor"), .height(16), .reset("Synchronous"), .scale(8), .width(16)) rgb_video_1: pin names not known; wires that end beside it: and_16_out, CLK, and_17_out, ScreenPos[3:0], ScreenPos[7:4], DATA

  // Notes on the sheet:
  //   contents of rom_2 (hex, n*v repeats v):
  //   90 0 6 0 0 0 40 10 ff 40 20 0 40 30 0 60 21 f3 60 31 f4 30 22 1 30 33 1 90 0 f
  //   Enable keboard
  //   Interrupts
  //   Disable CPU
endmodule

module REG_BANK (
  input  [7:0] DIN,
  input  [3:0] ADDR1,
  input  [3:0] ADDR2,
  input  [3:0] W_ADDR,
  input  WE,
  input  CLK,
  input  [6:0] Flag_In,
  input  Fin_sel,
  input  F_WE,
  output [7:0] O1,
  output [7:0] O2,
  output [7:0] O3,
  output [7:0] SPX_O,
  output [7:0] SPY_O,
  output [7:0] CSX_O,
  output [7:0] CSY_O,
  output [7:0] Status_o
);

  wire decoder_1_out1, decoder_1_out2, decoder_1_out3, decoder_1_out4, decoder_1_out5, decoder_1_out6,
       decoder_1_out7, decoder_1_out8, decoder_1_out9, decoder_1_out10, decoder_1_out11, decoder_1_out12,
       decoder_1_out13, decoder_1_out14, decoder_1_out15, undriven;
  wire [7:0] multiplexer_1_out, r1_q, r2_q, r3_q, r4_q, r5_q, r6_q, r7_q, r8_q, r9_q, ra_q;

  Decoder #(.select(4)) decoder_1 (
    .out1(decoder_1_out1), .out2(decoder_1_out2), .out3(decoder_1_out3), .out4(decoder_1_out4),
    .out5(decoder_1_out5), .out6(decoder_1_out6), .out7(decoder_1_out7), .out8(decoder_1_out8),
    .out9(decoder_1_out9), .out10(decoder_1_out10), .out11(decoder_1_out11), .out12(decoder_1_out12),
    .out13(decoder_1_out13), .out14(decoder_1_out14), .out15(decoder_1_out15), .sel(W_ADDR), .en(WE));  // open: out0
  Register r1 (.D(DIN), .en(decoder_1_out1), .clk(CLK), .Q(r1_q), .clr(undriven));
  Register r2 (.D(DIN), .en(decoder_1_out2), .clk(CLK), .Q(r2_q), .clr(undriven));
  Register r3 (.D(DIN), .en(decoder_1_out3), .clk(CLK), .Q(r3_q), .clr(undriven));
  Register r4 (.D(DIN), .en(decoder_1_out4), .clk(CLK), .Q(r4_q), .clr(undriven));
  Register r5 (.D(DIN), .en(decoder_1_out5), .clk(CLK), .Q(r5_q), .clr(undriven));
  Register r6 (.D(DIN), .en(decoder_1_out6), .clk(CLK), .Q(r6_q), .clr(undriven));
  Register r7 (.D(DIN), .en(decoder_1_out7), .clk(CLK), .Q(r7_q), .clr(undriven));
  Register r8 (.D(DIN), .en(decoder_1_out8), .clk(CLK), .Q(r8_q), .clr(undriven));
  Register r9 (.D(DIN), .en(decoder_1_out9), .clk(CLK), .Q(r9_q), .clr(undriven));
  Register ra (.D(DIN), .en(decoder_1_out10), .clk(CLK), .Q(ra_q), .clr(undriven));
  Register SPX (.D(DIN), .en(decoder_1_out12), .clk(CLK), .Q(SPX_O), .clr(undriven));
  Register SPY (.D(DIN), .en(decoder_1_out13), .clk(CLK), .Q(SPY_O), .clr(undriven));
  Register CSX (.D(DIN), .en(decoder_1_out14), .clk(CLK), .Q(CSX_O), .clr(undriven));
  Register CSY (.D(DIN), .en(decoder_1_out15), .clk(CLK), .Q(CSY_O), .clr(undriven));
  Multiplexer #(.width(8)) multiplexer_1 (.in0(DIN), .in1({1'b0, Flag_In}), .out(multiplexer_1_out), .sel(Fin_sel));
  Status_REG Stat_Reg (
    .WE(decoder_1_out11), .FWE(F_WE), .CLK(CLK), .R(undriven), .Din(multiplexer_1_out), .O(Status_o));
  Multiplexer #(.select(4), .width(8)) multiplexer_2 (
    .in0({8{1'b0}}), .in1(r1_q), .in2(r2_q), .in3(r3_q), .in4(r4_q), .in5(r5_q), .in6(r6_q), .in7(r7_q),
    .in8(r8_q), .in9(r9_q), .in10(ra_q), .in11(Status_o), .in12(SPX_O), .in13(SPY_O), .in14(CSX_O),
    .in15(CSY_O), .out(O1), .sel(ADDR1));
  Multiplexer #(.select(4), .width(8)) multiplexer_3 (
    .in0({8{1'b0}}), .in1(r1_q), .in2(r2_q), .in3(r3_q), .in4(r4_q), .in5(r5_q), .in6(r6_q), .in7(r7_q),
    .in8(r8_q), .in9(r9_q), .in10(ra_q), .in11(Status_o), .in12(SPX_O), .in13(SPY_O), .in14(CSX_O),
    .in15(CSY_O), .out(O2), .sel(ADDR2));
  Multiplexer #(.select(4), .width(8)) multiplexer_4 (
    .in0({8{1'b0}}), .in1(r1_q), .in2(r2_q), .in3(r3_q), .in4(r4_q), .in5(r5_q), .in6(r6_q), .in7(r7_q),
    .in8(r8_q), .in9(r9_q), .in10(ra_q), .in11(Status_o), .in12(SPX_O), .in13(SPY_O), .in14(CSX_O),
    .in15(CSY_O), .out(O3), .sel(W_ADDR));
endmodule

module Status_REG (
  input  [7:0] Din,
  input  WE,
  input  FWE,
  input  CLK,
  input  R,
  output [7:0] O
);

  wire [1:0] multiplexer_1_out;

  Multiplexer #(.select(2), .width(2)) multiplexer_1 (
    .in0(2'b00), .in1(2'b11), .in2(2'b01), .in3(2'b00), .out(multiplexer_1_out), .sel({FWE, WE}));
  Register #(.width(7)) flags (.D(Din[6:0]), .en(multiplexer_1_out[0]), .clk(CLK), .Q(O[6:0]), .clr(R));
  Register #(.width(1)) IRQE (.D(Din[7]), .en(multiplexer_1_out[1]), .clk(CLK), .Q(O[7]), .clr(R));
endmodule

module ALU (
  input  [7:0] A,
  input  [7:0] B,
  input  [3:0] OP,
  input  Cin,
  output [7:0] O,
  output Z,
  output Cout,
  output NulFlag,
  output Overflow,
  output Sign,
  output BT,
  output ST
);

  wire adder_1_cout, and_2_out, multiplexer_3_out, nor_2_out, or_2_out, or_3_out, subtractor_1_bout;
  wire [1:0] pla_1_out;
  wire [7:0] adder_1_out, and_1_out, multiplier_1_cout, multiplier_1_out, nand_1_out, negator_1_out,
       nor_1_out, or_1_out, shifter_1_out, shifter_2_out, shifter_3_out, shifter_4_out, subtractor_1_out,
       xnor_1_out, xor_1_out;

  Adder adder_1 (.a(A), .b(B), .out(adder_1_out), .cin(Cin), .cout(adder_1_cout));
  Subtractor subtractor_1 (.a(A), .b(B), .out(subtractor_1_out), .bin(Cin), .bout(subtractor_1_bout));
  Multiplier multiplier_1 (.a(A), .b(B), .out(multiplier_1_out), .cout(multiplier_1_cout));  // open: cin
  assign and_1_out = A & B;  // AND_Gate and_1, 8 bits wide
  assign or_1_out = A | B;  // OR_Gate or_1, 8 bits wide
  assign xor_1_out = A ^ B;  // XOR_Gate xor_1, 8 bits wide
  assign nand_1_out = ~(A & B);  // NAND_Gate nand_1, 8 bits wide
  assign nor_1_out = ~(A | B);  // NOR_Gate nor_1, 8 bits wide
  assign xnor_1_out = ~(A ^ B);  // XNOR_Gate xnor_1, 8 bits wide
  Shifter #(.shift("lr")) shifter_1 (.in(A), .\dist (B[2:0]), .out(shifter_1_out));
  Shifter #(.shift("ar")) shifter_2 (.in(A), .\dist (B[2:0]), .out(shifter_2_out));
  Shifter #(.shift("rl")) shifter_3 (.in(A), .\dist (B[2:0]), .out(shifter_3_out));
  Shifter #(.shift("rr")) shifter_4 (.in(A), .\dist (B[2:0]), .out(shifter_4_out));
  Negator negator_1 (.in(A), .out(negator_1_out));
  Comparator #(.mode("unsigned")) comparator_1 (.a(A), .b(B), .gt(BT), .lt(ST));  // open: eq
  Multiplexer #(.select(4), .width(8)) multiplexer_1 (
    .in0(adder_1_out), .in1(adder_1_out), .in2(subtractor_1_out), .in3(subtractor_1_out),
    .in4(multiplier_1_out), .in5(and_1_out), .in6(or_1_out), .in7(xor_1_out), .in8(nand_1_out),
    .in9(nor_1_out), .in10(xnor_1_out), .in11(shifter_1_out), .in12(shifter_2_out), .in13(shifter_3_out),
    .in14(shifter_4_out), .in15(negator_1_out), .out(O), .sel(OP));
  PLA #(.in_width(4), .\table ("0000 10 # add\n0001 10 # addc\n0010 11 # sub\n0011 11 # subc")) pla_1 (
    .in(OP), .out(pla_1_out));
  nor nor_2 (nor_2_out, OP[2], OP[3]);
  and and_2 (and_2_out, ~OP[0], ~OP[1]);  // AND_Gate
  Multiplexer #(.enable("true"), .select(2)) multiplexer_2 (
    .in0(adder_1_cout), .in1(subtractor_1_bout), .in2(or_2_out), .out(Overflow), .sel(OP[1:0]), .en(or_3_out));  // open: in3
  or or_2 (or_2_out, multiplier_1_cout[0], multiplier_1_cout[1], multiplier_1_cout[2], multiplier_1_cout[3], multiplier_1_cout[4], multiplier_1_cout[5], multiplier_1_cout[6], multiplier_1_cout[7]);
  or or_3 (or_3_out, nor_2_out, and_2_out);
  nor nor_3 (Z, O[0], O[1], O[2], O[3], O[4], O[5], O[6], O[7]);
  Multiplexer multiplexer_3 (.in0(adder_1_cout), .in1(subtractor_1_bout), .out(multiplexer_3_out), .sel(pla_1_out[0]));
  Multiplexer multiplexer_4 (.in0(1'b0), .in1(multiplexer_3_out), .out(Cout), .sel(pla_1_out[1]));

  assign NulFlag = 1'b0;
  assign Sign = O[7];
endmodule

module KP8B (
  input  [7:0] DIN,
  input  IRQ,
  input  NMI,
  input  RES,
  input  RDY,
  input  CLK,
  output [15:0] ADDR,
  output R_W,
  output CLKO,
  output [7:0] DOUT
);

  wire and_1_out, and_2_out, and_3_out, and_4_out, C_PC, d_ff_1_q, d_ff_2_q, F_We, Fin_Sel, Interrupt, L_PC,
       nor_1_out, or_1_out, or_2_out, or_3_out, or_4_out, R_PC, RA_Sel, RES_t, RES_UMC, RF_WE, s_r_ff_1_q,
       Shift_IR, TS_Shift;
  wire [1:0] B_SEL, OP_SEL;
  wire [2:0] ADDR_SEL, Bus_SEL, Micro_Seq;
  wire [2:1] RA_Control_out;
  wire [3:0] multiplexer_5_out, multiplexer_6_out, multiplexer_8_out, Specific_AC;
  wire [6:0] A_L_U_z;
  wire [7:0] A_L_U_o, IR_p3, multiplexer_7_out, not_1_out, Registers_o3, Status, undriven, undriven_2;
  wire [8:8] multiplexer_1_out;
  wire [15:0] CStack_Pointer, PC, Registers_o2, Stack_Pointer;
  wire [23:0] IR;

  and and_1 (and_1_out, ~IR[20], IR[21], IR[22], IR[23]);  // AND_Gate
  or or_1 (or_1_out, ~and_1_out, Interrupt);  // OR_Gate
  and and_2 (and_2_out, IRQ, Status[7]);
  D_Flip_Flop d_ff_1 (.D(RES), .clk(CLK), .Q(d_ff_1_q));  // open: Qn, preset, reset
  D_Flip_Flop d_ff_2 (.D(and_3_out), .clk(CLK), .Q(d_ff_2_q));  // open: Qn, preset, reset
  and and_3 (and_3_out, RDY, or_1_out);
  or or_2 (or_2_out, and_2_out, NMI);
  and and_4 (and_4_out, IR[20], ~IR[21], ~IR[22], ~IR[23]);  // AND_Gate
  and and_5 (CLKO, d_ff_2_q, CLK);
  S_R_Flip_Flop s_r_ff_1 (.clk(CLK), .Q(s_r_ff_1_q), .reset(and_4_out), .preset(or_2_out));  // open: S, R, Qn
  and and_6 (RES_t, d_ff_1_q, CLK, Shift_IR);
  and and_7 (Interrupt, s_r_ff_1_q, nor_1_out);
  nor nor_1 (nor_1_out, Micro_Seq[0], Micro_Seq[1], Micro_Seq[2]);
  assign not_1_out = ~Status;  // NOT_Gate not_1, 8 bits wide
  Multiplexer #(.select(4)) multiplexer_1 (
    .in0(Status[0]), .in1(Status[1]), .in2(Status[2]), .in3(Status[3]), .in4(Status[4]), .in5(Status[5]),
    .in6(Status[6]), .in7(Status[7]), .in8(not_1_out[0]), .in9(not_1_out[1]), .in10(not_1_out[2]),
    .in11(not_1_out[3]), .in12(not_1_out[4]), .in13(not_1_out[5]), .in14(not_1_out[6]), .in15(not_1_out[7]),
    .out(multiplexer_1_out[8]), .sel(IR[19:16]));
  or or_3 (or_3_out, RES_t, RES_UMC);
  Counter #(.max('h7), .width(3)) counter_1 (
    .load(1'b0), .count(1'b1), .Q(Micro_Seq), .up(1'b1), .clk(CLKO), .clr(or_3_out));  // open: D, carry
  PLA #(.in_width(9), .out_width(20), .\table ("xxxxxx000 00000000000000010010 # FETCH\nxxxxxx001 00000000000000010010 # FETCH\nxxxxxx010 00000000000000010010 # FETCH\nx0000x011 00000000000000000001 # NOP\nx0011x011 00010000000110100000 # ALUI\nx0011x100 00000000000000000001 # ALUI\nx0010x011 00000000000110100000 # ALU\nx0010x100 00000000000000000001 # ALU\nx0100x011 00000001010000100000 # LDI\nx0100x100 00000000000000000001 # LDI\nx1001x011 00000010000000001000 # JMP\nx1001x100 00000000000000000001 # JMP\n11010x011 00000010000000001000 # JF\n11010x100 00000000000000000001 # JF\nx1011x011 00000110000000001000 # RJM\nx1011x100 00000000000000000001 # RJM\nx01100011 00000100100001000000 # STR\nx01100100 00000000000000000001 # STR\nx01101011 00000110100001000000 # STRY\nx01101100 00000000000000000001 # STRY\nx01010011 00000100010000100000 # LOD\nx01010100 00000000000000000001 # LOD\nx01011011 00000110010000100000 # LODY\nx01011100 00000000000000000001 # LODY\nx11110011 00000010100001000000 # STA\nx11110100 00000000000000000001 # STA\nx11111011 00000010010000100000 # LDA\nx11111100 00000000000000000001 # LDA\nx1110x011 00000000000000000000 # WAIT\nx1110x100 00000000000000000001 # WAIT\nx0111x011 00001000100001000000 # PSH\nx0111x100 10110000000000100000 # PSH\nx0111x101 00000000000000000001 # PSH\nx1000x011 00001000010000100000 # POP\nx1000x100 01110000000000100000 # POP\nx1000x101 00000000000000000001 # POP\nx1100x011 00001010110001000000 # CALL\nx1100x100 10110000000000100000 # CALL\nx1100x101 00001011000001000000 # CALL\nx1100x110 10110000000000100000 # CALL\nx1100x111 00000010000000001000 # CALL\nx1101x011 00001010011000000000 # RET\nx1101x100 01110000000000100000 # RET\nx1101x101 00001010011000000000 # RET\nx1101x110 01110000000000100000 # RET\nx1101x111 00001100000000001000 # RET\nx0001x011 00001010110001000000 # BRK\nx0001x100 10110000000000100000 # BRK\nx0001x101 00001010110001000000 # BRK\nx0001x110 10110000000000100000 # BRK\nx0001x111 00001110000000001000 # BRK")) Instruction_Decoder (
    .in({multiplexer_1_out[8], IR[23:19], Micro_Seq}),
    .out({OP_SEL, B_SEL, ADDR_SEL, Bus_SEL, TS_Shift, Fin_Sel, F_We, R_W, RF_WE, C_PC, L_PC, R_PC, Shift_IR, RES_UMC}));
  Counter #(.max('hffff), .width(16)) counter_2 (
    .load(L_PC), .D(ADDR), .count(C_PC), .Q(PC), .up(1'b1), .clk(CLKO), .clr(or_4_out));  // open: carry
  Multiplexer #(.select(3), .width(16)) multiplexer_2 (
    .in0(PC), .in1(IR[15:0]), .in2({Registers_o2[15:8], IR[7:0]}), .in3(Registers_o2), .in4(Stack_Pointer),
    .in5(CStack_Pointer), .in6({undriven_2, undriven}), .in7(16'h3), .out(ADDR), .sel(ADDR_SEL));
  or or_4 (or_4_out, RES_t, R_PC);
  Multiplexer #(.select(3), .width(8)) multiplexer_3 (
    .in0(A_L_U_o), .in1(DIN), .in2(Registers_o3), .in3(PC[7:0]), .in4(PC[15:8]), .in5(IR[7:0]), .out(DOUT),
    .sel(Bus_SEL));  // open: in6, in7
  // Shift_Register #(.length(3), .width(8)) IR: pin names not known; wires that end beside it: Shift_IR, CLKO, IR_p3
  Multiplexer #(.width(8)) multiplexer_4 (.in0(DIN), .in1(8'h10), .out(IR_p3), .sel(Interrupt));
  // Shift_Register #(.length(2), .width(8)) Temp_shift: pin names not known; wires that end beside it: TS_Shift, CLKO, DOUT
  Multiplexer #(.width(4)) multiplexer_5 (.in0(IR[15:12]), .in1(Specific_AC), .out(multiplexer_5_out), .sel(RA_Sel));
  Multiplexer #(.width(4)) multiplexer_6 (.in0(IR[11:8]), .in1(Specific_AC), .out(multiplexer_6_out), .sel(RA_Sel));
  REG_BANK Registers (
    .WE(RF_WE), .CLK(CLKO), .ADDR1(multiplexer_6_out), .ADDR2(IR[3:0]), .W_ADDR(multiplexer_5_out),
    .DIN(DOUT), .Flag_In(A_L_U_z), .Fin_sel(Fin_Sel), .F_WE(F_We), .O1(Registers_o2[15:8]),
    .O2(Registers_o2[7:0]), .O3(Registers_o3), .SPX_O(Stack_Pointer[7:0]), .SPY_O(Stack_Pointer[15:8]),
    .CSX_O(CStack_Pointer[7:0]), .CSY_O(CStack_Pointer[15:8]), .Status_o(Status));
  PLA #(.in_width(7), .out_width(3), .\table ("1000111 001 # psh\n1001000 001 # pop\n1001100 011 # call\n1001101 011 # ret\n0111111 101 # sta/lda\n1011100 011 # call\n1101101 011 # ret\n1000001 011 # brk\n1010001 011 # brk")) RA_Control (
    .in({Micro_Seq, IR[23:20]}), .out({RA_Control_out, RA_Sel}));
  Multiplexer #(.select(2), .width(8)) multiplexer_7 (
    .in0(Registers_o2[7:0]), .in1(IR[7:0]), .in2(IR[11:4]), .in3(8'h1), .out(multiplexer_7_out), .sel(B_SEL));
  Multiplexer #(.select(2), .width(4)) multiplexer_8 (
    .in0(IR[19:16]), .in1(4'b0000), .in2(4'b0010), .out(multiplexer_8_out), .sel(OP_SEL));  // open: in3
  Multiplexer #(.select(2), .width(4)) multiplexer_9 (
    .in0(4'b1100), .in1(4'b1110), .in2(4'b1010), .out(Specific_AC), .sel(RA_Control_out));  // open: in3
  ALU A_L_U (
    .A(Registers_o2[15:8]), .B(multiplexer_7_out), .OP(multiplexer_8_out), .Cin(Status[1]), .O(A_L_U_o),
    .Z(A_L_U_z[0]), .Cout(A_L_U_z[1]), .NulFlag(A_L_U_z[2]), .Overflow(A_L_U_z[3]), .Sign(A_L_U_z[4]),
    .BT(A_L_U_z[5]), .ST(A_L_U_z[6]));

  // Other names for the same wires on the sheet: M2 = R_W; CLK_t = CLKO

  // Notes on the sheet:
  //   RDY: initial=0x1
endmodule
