// Logisim project KP8B_CPU.circ as structural Verilog: 6 circuits, main circuit KP8B
module REG_BANK (
  input  [7:0] DIN,
  input  [3:0] ADDR1,
  input  [3:0] ADDR2,
  input  [3:0] W_ADDR,
  input  WE,
  input  CLK,
  input  [5:0] Flag_In,
  input  Fin_sel,
  input  F_WE,
  output [7:0] O1,
  output [7:0] O2,
  output [7:0] O3,
  output [7:0] SPX_O,
  output [7:0] SPY_O,
  output [7:0] CSX_O,
  output [7:0] CSY_O,
  output [7:0] Status_o
);

  wire decoder_1_out1, decoder_1_out2, decoder_1_out3, decoder_1_out4, decoder_1_out5, decoder_1_out6,
       decoder_1_out7, decoder_1_out8, decoder_1_out9, decoder_1_out10, decoder_1_out11, decoder_1_out12,
       decoder_1_out13, decoder_1_out14, decoder_1_out15, undriven;
  wire [7:0] multiplexer_1_out, r1_q, r2_q, r3_q, r4_q, r5_q, r6_q, r7_q, r8_q, r9_q, ra_q;

  Decoder #(.select(4)) decoder_1 (
    .out1(decoder_1_out1), .out2(decoder_1_out2), .out3(decoder_1_out3), .out4(decoder_1_out4),
    .out5(decoder_1_out5), .out6(decoder_1_out6), .out7(decoder_1_out7), .out8(decoder_1_out8),
    .out9(decoder_1_out9), .out10(decoder_1_out10), .out11(decoder_1_out11), .out12(decoder_1_out12),
    .out13(decoder_1_out13), .out14(decoder_1_out14), .out15(decoder_1_out15), .sel(W_ADDR), .en(WE));  // open: out0
  Register r1 (.D(DIN), .en(decoder_1_out1), .clk(CLK), .Q(r1_q), .clr(undriven));
  Register r2 (.D(DIN), .en(decoder_1_out2), .clk(CLK), .Q(r2_q), .clr(undriven));
  Register r3 (.D(DIN), .en(decoder_1_out3), .clk(CLK), .Q(r3_q), .clr(undriven));
  Register r4 (.D(DIN), .en(decoder_1_out4), .clk(CLK), .Q(r4_q), .clr(undriven));
  Register r5 (.D(DIN), .en(decoder_1_out5), .clk(CLK), .Q(r5_q), .clr(undriven));
  Register r6 (.D(DIN), .en(decoder_1_out6), .clk(CLK), .Q(r6_q), .clr(undriven));
  Register r7 (.D(DIN), .en(decoder_1_out7), .clk(CLK), .Q(r7_q), .clr(undriven));
  Register r8 (.D(DIN), .en(decoder_1_out8), .clk(CLK), .Q(r8_q), .clr(undriven));
  Register r9 (.D(DIN), .en(decoder_1_out9), .clk(CLK), .Q(r9_q), .clr(undriven));
  Register ra (.D(DIN), .en(decoder_1_out10), .clk(CLK), .Q(ra_q), .clr(undriven));
  Register SPX (.D(DIN), .en(decoder_1_out12), .clk(CLK), .Q(SPX_O), .clr(undriven));
  Register SPY (.D(DIN), .en(decoder_1_out13), .clk(CLK), .Q(SPY_O), .clr(undriven));
  Register CSX (.D(DIN), .en(decoder_1_out14), .clk(CLK), .Q(CSX_O), .clr(undriven));
  Register CSY (.D(DIN), .en(decoder_1_out15), .clk(CLK), .Q(CSY_O), .clr(undriven));
  Multiplexer #(.width(8)) multiplexer_1 (.in0(DIN), .in1({2'b00, Flag_In}), .out(multiplexer_1_out), .sel(Fin_sel));
  Status_REG Stat_Reg (
    .WE(decoder_1_out11), .FWE(F_WE), .CLK(CLK), .R(undriven), .Din(multiplexer_1_out), .O(Status_o));
  Multiplexer #(.select(4), .width(8)) multiplexer_2 (
    .in0({8{1'b0}}), .in1(r1_q), .in2(r2_q), .in3(r3_q), .in4(r4_q), .in5(r5_q), .in6(r6_q), .in7(r7_q),
    .in8(r8_q), .in9(r9_q), .in10(ra_q), .in11(Status_o), .in12(SPX_O), .in13(SPY_O), .in14(CSX_O),
    .in15(CSY_O), .out(O1), .sel(ADDR1));
  Multiplexer #(.select(4), .width(8)) multiplexer_3 (
    .in0({8{1'b0}}), .in1(r1_q), .in2(r2_q), .in3(r3_q), .in4(r4_q), .in5(r5_q), .in6(r6_q), .in7(r7_q),
    .in8(r8_q), .in9(r9_q), .in10(ra_q), .in11(Status_o), .in12(SPX_O), .in13(SPY_O), .in14(CSX_O),
    .in15(CSY_O), .out(O2), .sel(ADDR2));
  Multiplexer #(.select(4), .width(8)) multiplexer_4 (
    .in0({8{1'b0}}), .in1(r1_q), .in2(r2_q), .in3(r3_q), .in4(r4_q), .in5(r5_q), .in6(r6_q), .in7(r7_q),
    .in8(r8_q), .in9(r9_q), .in10(ra_q), .in11(Status_o), .in12(SPX_O), .in13(SPY_O), .in14(CSX_O),
    .in15(CSY_O), .out(O3), .sel(W_ADDR));
endmodule

module Status_REG (
  input  [7:0] Din,
  input  WE,
  input  FWE,
  input  CLK,
  input  R,
  output [7:0] O
);

  wire [1:0] multiplexer_1_out;

  Multiplexer #(.select(2), .width(2)) multiplexer_1 (
    .in0(2'b00), .in1(2'b11), .in2(2'b01), .in3(2'b00), .out(multiplexer_1_out), .sel({FWE, WE}));
  Register #(.width(6)) flags (.D(Din[5:0]), .en(multiplexer_1_out[0]), .clk(CLK), .Q(O[5:0]), .clr(R));
  Register #(.width(2)) IRQE (.D(Din[7:6]), .en(multiplexer_1_out[1]), .clk(CLK), .Q(O[7:6]), .clr(R));
endmodule

module ALU (
  input  [7:0] A,
  input  [7:0] B,
  input  [3:0] OP,
  input  Cin,
  input  [7:0] in_5,
  input  BCD,
  output [7:0] O,
  output Z,
  output Overflow,
  output Sign,
  output Cout,
  output BT,
  output ST
);

  wire adder_1_cout, and_3_out, bcdadder_1_cout, bcdsubtractor_1_bout, Cenable_out, Cin_t, multiplexer_3_out,
       multiplexer_5_out, multiplexer_7_out, nor_2_out, or_2_out, or_3_out, or_4_out, subtractor_1_bout;
  wire [1:0] Ov_Sel_out;
  wire [2:0] C_Sel_out;
  wire [7:0] adder_1_out, and_2_out, bcdadder_1_o, bcdsubtractor_1_o, multiplexer_2_out, multiplexer_4_out,
       multiplier_1_cout, multiplier_1_out, nand_1_out, nor_1_out, or_1_out, subtractor_1_out, xnor_1_out,
       xor_1_out;

  PLA #(.in_width(4), .out_width(1), .\table ("0001 1 # addc\n0010 1 # subc\n1111 1 # shrc")) Cenable (
    .in(OP), .out(Cenable_out));
  and and_1 (Cin_t, Cin, Cenable_out);
  Adder adder_1 (.a(A), .b(B), .out(adder_1_out), .cin(Cin_t), .cout(adder_1_cout));
  Subtractor subtractor_1 (.a(A), .b(B), .out(subtractor_1_out), .bin(Cin_t), .bout(subtractor_1_bout));
  Multiplier multiplier_1 (.a(A), .b(B), .out(multiplier_1_out), .cout(multiplier_1_cout));  // open: cin
  assign and_2_out = A & B;  // AND_Gate and_2, 8 bits wide
  assign or_1_out = A | B;  // OR_Gate or_1, 8 bits wide
  assign xor_1_out = A ^ B;  // XOR_Gate xor_1, 8 bits wide
  assign nand_1_out = ~(A & B);  // NAND_Gate nand_1, 8 bits wide
  assign nor_1_out = ~(A | B);  // NOR_Gate nor_1, 8 bits wide
  assign xnor_1_out = ~(A ^ B);  // XNOR_Gate xnor_1, 8 bits wide
  Comparator #(.mode("unsigned")) comparator_1 (.a(A), .b(B), .gt(BT), .lt(ST));  // open: eq
  or or_2 (or_2_out, A[0], A[0]);
  BCDADDER bcdadder_1 (.A(A), .B(B), .Cin(Cin_t), .O(bcdadder_1_o), .Cout(bcdadder_1_cout));
  BCDSUBTRACTOR bcdsubtractor_1 (.A(A), .B(B), .Bin(Cin_t), .Bout(bcdsubtractor_1_bout), .O(bcdsubtractor_1_o));
  Multiplexer #(.select(4), .width(8)) multiplexer_1 (
    .in0(multiplexer_2_out), .in1(multiplexer_2_out), .in2(multiplexer_4_out), .in3(multiplexer_4_out),
    .in4(multiplier_1_out), .in5(and_2_out), .in6(or_1_out), .in7(xor_1_out), .in8(nand_1_out),
    .in9(nor_1_out), .in10(xnor_1_out), .in11({Cin_t, A[7:1]}), .in12({A[7], 1'b0, A[6:1]}),
    .in13({in_5[6:0], in_5[7]}), .in14({A[0], A[7:1]}), .in15({Cin_t, A[7:1]}), .out(O), .sel(OP));
  Multiplexer #(.width(8)) multiplexer_2 (.in0(adder_1_out), .in1(bcdadder_1_o), .out(multiplexer_2_out), .sel(BCD));
  Multiplexer multiplexer_3 (.in0(adder_1_cout), .in1(bcdadder_1_cout), .out(multiplexer_3_out), .sel(BCD));
  Multiplexer #(.width(8)) multiplexer_4 (
    .in0(subtractor_1_out), .in1(bcdsubtractor_1_o), .out(multiplexer_4_out), .sel(BCD));
  Multiplexer multiplexer_5 (.in0(subtractor_1_bout), .in1(bcdsubtractor_1_bout), .out(multiplexer_5_out), .sel(BCD));
  PLA #(.in_width(4), .out_width(3), .\table ("0000 100 # add\n0001 100 # addc\n0010 101 # sub\n0011 101 # subc\n1011 110 # shr\n1111 111 # shrc\n1100 110 # asr")) C_Sel (
    .in(OP), .out(C_Sel_out));
  PLA #(.in_width(4), .\table ("0000 00 # add\n0001 00 # addc\n0010 01 # sub\n0011 01 # subc\n0100 10 # mult\n1011 11 # shr\n1100 11 # asr\n1111 11 # shrc")) Ov_Sel (
    .in(OP), .out(Ov_Sel_out));
  nor nor_2 (nor_2_out, OP[2], OP[3]);
  and and_3 (and_3_out, ~OP[0], ~OP[1]);  // AND_Gate
  or or_3 (or_3_out, multiplier_1_cout[0], multiplier_1_cout[1], multiplier_1_cout[2], multiplier_1_cout[3], multiplier_1_cout[4], multiplier_1_cout[5], multiplier_1_cout[6], multiplier_1_cout[7]);
  or or_4 (or_4_out, nor_2_out, and_3_out);
  Multiplexer #(.enable("true"), .select(2)) multiplexer_6 (
    .in0(multiplexer_3_out), .in1(multiplexer_5_out), .in2(or_3_out), .in3(or_2_out), .out(Overflow),
    .sel(Ov_Sel_out), .en(or_4_out));
  nor nor_3 (Z, O[0], O[1], O[2], O[3], O[4], O[5], O[6], O[7]);
  Multiplexer #(.select(2)) multiplexer_7 (
    .in0(multiplexer_3_out), .in1(multiplexer_5_out), .in2(or_2_out), .in3(A[0]), .out(multiplexer_7_out),
    .sel(C_Sel_out[1:0]));
  Multiplexer multiplexer_8 (.in0(1'b0), .in1(multiplexer_7_out), .out(Cout), .sel(C_Sel_out[2]));

  assign Sign = O[7];
endmodule

module KP8B (
  input  [7:0] DIN,
  input  IRQ,
  input  NMI,
  input  RES,
  input  RDY,
  input  CLK,
  output [15:0] ADDR,
  output R_W,
  output CLKO,
  output [7:0] DOUT,
  output IIP,
  output INWAIT,
  output MRB
);

  wire and_1_out, and_2_out, and_3_out, and_4_out, and_5_out, C_PC, d_ff_1_q, d_ff_2_q, F_We, Fin_Sel,
       Interrupt, L_PC, mrbSEL_out, nor_1_out, or_1_out, or_2_out, or_3_out, or_5_out, R_PC, RA_Sel, RES_t,
       RES_UMC, RF_WE, s_r_ff_2_q, Shift_IR, TS_Shift;
  wire [1:0] B_SEL, OP_SEL;
  wire [2:0] ADDR_SEL, Bus_SEL, Micro_Seq;
  wire [2:1] RA_Control_out;
  wire [3:0] multiplexer_5_out, multiplexer_6_out, multiplexer_8_out, Specific_AC;
  wire [5:0] A_L_U_z;
  wire [7:0] A_L_U_o, IR_p3, multiplexer_7_out, not_1_out, Registers_o3, Status, undriven, undriven_2;
  wire [7:1] undriven_3;
  wire [8:8] multiplexer_1_out;
  wire [15:0] CStack_Pointer, PC, Registers_o2, Stack_Pointer;
  wire [23:0] IR;

  and and_1 (and_1_out, ~IR[20], IR[21], IR[22], IR[23]);  // AND_Gate
  or or_1 (or_1_out, ~and_1_out, Interrupt);  // OR_Gate
  and and_2 (and_2_out, IRQ, Status[7]);
  D_Flip_Flop d_ff_1 (.D(RES), .clk(CLK), .Q(d_ff_1_q));  // open: Qn, preset, reset
  D_Flip_Flop d_ff_2 (.D(and_3_out), .clk(CLK), .Q(d_ff_2_q));  // open: Qn, preset, reset
  and and_3 (and_3_out, RDY, or_1_out);
  and and_4 (and_4_out, IR[20], IR[21], ~IR[22], ~IR[23]);  // AND_Gate
  or or_2 (or_2_out, and_2_out, NMI);
  and and_5 (and_5_out, IR[20], ~IR[21], ~IR[22], ~IR[23]);  // AND_Gate
  and and_6 (CLKO, d_ff_2_q, CLK);
  S_R_Flip_Flop s_r_ff_1 (.Q(IIP), .reset(and_4_out), .preset(or_2_out));  // open: S, R, clk, Qn
  S_R_Flip_Flop s_r_ff_2 (.clk(CLK), .Q(s_r_ff_2_q), .reset(and_5_out), .preset(or_2_out));  // open: S, R, Qn
  and and_7 (RES_t, d_ff_1_q, CLK, Shift_IR);
  and and_8 (Interrupt, s_r_ff_2_q, nor_1_out);
  nor nor_1 (nor_1_out, Micro_Seq[0], Micro_Seq[1], Micro_Seq[2]);
  assign not_1_out = ~Status;  // NOT_Gate not_1, 8 bits wide
  Multiplexer #(.select(4)) multiplexer_1 (
    .in0(Status[0]), .in1(Status[1]), .in2(Status[2]), .in3(Status[3]), .in4(Status[4]), .in5(Status[5]),
    .in6(Status[6]), .in7(Status[7]), .in8(not_1_out[0]), .in9(not_1_out[1]), .in10(not_1_out[2]),
    .in11(not_1_out[3]), .in12(not_1_out[4]), .in13(not_1_out[5]), .in14(not_1_out[6]), .in15(not_1_out[7]),
    .out(multiplexer_1_out[8]), .sel(IR[19:16]));
  and and_9 (INWAIT, ~IR[20], IR[21], IR[22], IR[23]);  // AND_Gate
  or or_3 (or_3_out, RES_t, RES_UMC);
  Counter #(.max('h7), .width(3)) counter_1 (
    .load(1'b0), .count(1'b1), .Q(Micro_Seq), .up(1'b1), .clk(CLKO), .clr(or_3_out));  // open: D, carry
  PLA #(.in_width(9), .out_width(20), .\table ("xxxxxx000 00000000000000010010 # FETCH\nxxxxxx001 00000000000000010010 # FETCH\nxxxxxx010 00000000000000010010 # FETCH\nx0000x011 00000000000000000001 # NOP\nx0011x011 00010000000110100000 # ALUI\nx0011x100 00000000000000000001 # ALUI\nx0010x011 00000000000110100000 # ALU\nx0010x100 00000000000000000001 # ALU\nx0100x011 00000001010000100000 # LDI\nx0100x100 00000000000000000001 # LDI\nx1001x011 00000010000000001000 # JMP\nx1001x100 00000000000000000001 # JMP\n11010x011 00000010000000001000 # JF\n11010x100 00000000000000000001 # JF\nx1011x011 00000110000000001000 # RJM\nx1011x100 00000000000000000001 # RJM\nx01100011 00000100100001000000 # STR\nx01100100 00000000000000000001 # STR\nx01101011 00000110100001000000 # STRY\nx01101100 00000000000000000001 # STRY\nx01010011 00000100010000100000 # LOD\nx01010100 00000000000000000001 # LOD\nx01011011 00000110010000100000 # LODY\nx01011100 00000000000000000001 # LODY\nx11110011 00000010100001000000 # STA\nx11110100 00000000000000000001 # STA\nx11111011 00000010010000100000 # LDA\nx11111100 00000000000000000001 # LDA\nx1110x011 00000000000000000000 # WAIT\nx1110x100 00000000000000000001 # WAIT\nx0111x011 00001000100001000000 # PSH\nx0111x100 10110000000000100000 # PSH\nx0111x101 00000000000000000001 # PSH\nx1000x011 00001000010000100000 # POP\nx1000x100 01110000000000100000 # POP\nx1000x101 00000000000000000001 # POP\nx1100x011 00001010110001000000 # CALL\nx1100x100 10110000000000100000 # CALL\nx1100x101 00001011000001000000 # CALL\nx1100x110 10110000000000100000 # CALL\nx1100x111 00000010000000001000 # CALL\nx1101x011 00001010011000000000 # RET\nx1101x100 01110000000000100000 # RET\nx1101x101 00001010011000000000 # RET\nx1101x110 01110000000000100000 # RET\nx1101x111 00001100000000001000 # RET\nx0001x011 00001010110001000000 # BRK\nx0001x100 10110000000000100000 # BRK\nx0001x101 00001010110001000000 # BRK\nx0001x110 10110000000000100000 # BRK\nx0001x111 00001110000000001000 # BRK")) Instruction_Decoder (
    .in({multiplexer_1_out[8], IR[23:19], Micro_Seq}),
    .out({OP_SEL, B_SEL, ADDR_SEL, Bus_SEL, TS_Shift, Fin_Sel, F_We, R_W, RF_WE, C_PC, L_PC, R_PC, Shift_IR, RES_UMC}));
  PLA #(.in_width(4), .out_width(1), .\table ("0110 1 # STR\n0101 1 # LOD\n0111 1 # PSH\n1000 1 # POP\n1100 1 # CALL\n1101 1 # RET\n1111 1 # STA/LDA\n0001 1 # BRK")) mrbSEL (
    .in(IR[23:20]), .out(mrbSEL_out));
  Counter #(.max('hffff), .width(16)) counter_2 (
    .load(L_PC), .D(ADDR), .count(C_PC), .Q(PC), .up(1'b1), .clk(CLKO), .clr(or_5_out));  // open: carry
  Multiplexer #(.select(3), .width(16)) multiplexer_2 (
    .in0(PC), .in1(IR[15:0]), .in2({Registers_o2[15:8], IR[7:0]}), .in3(Registers_o2), .in4(Stack_Pointer),
    .in5(CStack_Pointer), .in6({undriven_2, undriven}), .in7(16'h3), .out(ADDR), .sel(ADDR_SEL));
  or or_4 (MRB, Shift_IR, mrbSEL_out);
  or or_5 (or_5_out, RES_t, R_PC);
  Multiplexer #(.select(3), .width(8)) multiplexer_3 (
    .in0(A_L_U_o), .in1(DIN), .in2(Registers_o3), .in3(PC[7:0]), .in4(PC[15:8]), .in5(IR[7:0]), .out(DOUT),
    .sel(Bus_SEL));  // open: in6, in7
  // Shift_Register #(.length(3), .width(8)) IR: pin names not known; wires that end beside it: Shift_IR, CLKO, IR_p3
  Multiplexer #(.width(8)) multiplexer_4 (.in0(DIN), .in1(8'h10), .out(IR_p3), .sel(Interrupt));
  // Shift_Register #(.length(2), .width(8)) Temp_shift: pin names not known; wires that end beside it: TS_Shift, CLKO, DOUT
  Multiplexer #(.width(4)) multiplexer_5 (.in0(IR[15:12]), .in1(Specific_AC), .out(multiplexer_5_out), .sel(RA_Sel));
  Multiplexer #(.width(4)) multiplexer_6 (.in0(IR[11:8]), .in1(Specific_AC), .out(multiplexer_6_out), .sel(RA_Sel));
  REG_BANK Registers (
    .WE(RF_WE), .CLK(CLKO), .ADDR1(multiplexer_6_out), .ADDR2(IR[3:0]), .W_ADDR(multiplexer_5_out),
    .DIN(DOUT), .Flag_In(A_L_U_z), .Fin_sel(Fin_Sel), .F_WE(F_We), .O1(Registers_o2[15:8]),
    .O2(Registers_o2[7:0]), .O3(Registers_o3), .SPX_O(Stack_Pointer[7:0]), .SPY_O(Stack_Pointer[15:8]),
    .CSX_O(CStack_Pointer[7:0]), .CSY_O(CStack_Pointer[15:8]), .Status_o(Status));
  PLA #(.in_width(7), .out_width(3), .\table ("1000111 001 # psh\n1001000 001 # pop\n1001100 011 # call\n1001101 011 # ret\n0111111 101 # sta/lda\n1011100 011 # call\n1101101 011 # ret\n1000001 011 # brk\n1010001 011 # brk")) RA_Control (
    .in({Micro_Seq, IR[23:20]}), .out({RA_Control_out, RA_Sel}));
  Multiplexer #(.select(2), .width(8)) multiplexer_7 (
    .in0(Registers_o2[7:0]), .in1(IR[7:0]), .in2(IR[11:4]), .in3(8'h1), .out(multiplexer_7_out), .sel(B_SEL));
  Multiplexer #(.select(2), .width(4)) multiplexer_8 (
    .in0(IR[19:16]), .in1(4'b0000), .in2(4'b0010), .out(multiplexer_8_out), .sel(OP_SEL));  // open: in3
  Multiplexer #(.select(2), .width(4)) multiplexer_9 (
    .in0(4'b1100), .in1(4'b1110), .in2(4'b1010), .out(Specific_AC), .sel(RA_Control_out));  // open: in3
  ALU A_L_U (
    .A(Registers_o2[15:8]), .B(multiplexer_7_out), .OP(multiplexer_8_out), .Cin(Status[0]),
    .in_5({undriven_3, Status[6]}), .BCD(Status[6]), .O(A_L_U_o), .Z(A_L_U_z[0]), .Overflow(A_L_U_z[1]),
    .Sign(A_L_U_z[2]), .Cout(A_L_U_z[3]), .BT(A_L_U_z[4]), .ST(A_L_U_z[5]));
  // Pins of 1 and 8 bits meet at {undriven_3, Status[6]}

  // Other names for the same wires on the sheet: M2 = R_W; CLK_t = CLKO

  // Notes on the sheet:
  //   RDY: initial=0x1
endmodule

module BCDADDER (
  input  Cin,
  input  [7:0] A,
  input  [7:0] B,
  output [7:0] O,
  output Cout
);

  wire adder_1_cout, adder_2_cout, adder_3_cout, and_1_out, and_2_out, and_3_out, and_4_out, or_1_out;
  wire [2:2] or_2_out, or_3_out;
  wire [3:0] adder_1_out, adder_2_out;

  Adder #(.width(4)) adder_1 (.a(A[3:0]), .b(B[3:0]), .out(adder_1_out), .cin(Cin), .cout(adder_1_cout));
  or or_1 (or_1_out, adder_1_cout, adder_3_cout);
  Adder #(.width(4)) adder_2 (.a(A[7:4]), .b(B[7:4]), .out(adder_2_out), .cin(or_1_out), .cout(adder_2_cout));
  Adder #(.width(4)) adder_3 (
    .a(adder_1_out), .b({1'b0, {2{or_2_out[2]}}, 1'b0}), .out(O[3:0]), .cin(1'b0), .cout(adder_3_cout));
  Adder #(.width(4)) adder_4 (
    .a(adder_2_out), .b({1'b0, {2{or_3_out[2]}}, 1'b0}), .out(O[7:4]), .cin(1'b0), .cout(Cout));
  and and_1 (and_1_out, adder_1_out[2], adder_1_out[3]);
  and and_2 (and_2_out, adder_1_out[1], adder_1_out[3]);
  and and_3 (and_3_out, adder_2_out[2], adder_2_out[3]);
  and and_4 (and_4_out, adder_2_out[1], adder_2_out[3]);
  or or_2 (or_2_out[2], and_1_out, and_2_out, adder_1_cout);
  or or_3 (or_3_out[2], and_3_out, and_4_out, adder_2_cout);
endmodule

module BCDSUBTRACTOR (
  input  Bin,
  input  [7:0] A,
  input  [7:0] B,
  output [7:0] O,
  output Bout
);

  wire and_1_out, and_2_out, and_3_out, and_4_out, or_1_out, subtractor_1_bout, subtractor_2_bout,
       subtractor_3_bout;
  wire [2:2] or_2_out, or_3_out;
  wire [3:0] subtractor_1_out, subtractor_2_out;

  Subtractor #(.width(4)) subtractor_1 (
    .a(A[3:0]), .b(B[3:0]), .out(subtractor_1_out), .bin(Bin), .bout(subtractor_1_bout));
  or or_1 (or_1_out, subtractor_1_bout, subtractor_3_bout);
  Subtractor #(.width(4)) subtractor_2 (
    .a(A[7:4]), .b(B[7:4]), .out(subtractor_2_out), .bin(or_1_out), .bout(subtractor_2_bout));
  Subtractor #(.width(4)) subtractor_3 (
    .a(subtractor_1_out), .b({1'b0, {2{or_2_out[2]}}, 1'b0}), .out(O[3:0]), .bin(1'b0),
    .bout(subtractor_3_bout));
  Subtractor #(.width(4)) subtractor_4 (
    .a(subtractor_2_out), .b({1'b0, {2{or_3_out[2]}}, 1'b0}), .out(O[7:4]), .bin(1'b0), .bout(Bout));
  and and_1 (and_1_out, subtractor_1_out[2], subtractor_1_out[3]);
  and and_2 (and_2_out, subtractor_1_out[1], subtractor_1_out[3]);
  and and_3 (and_3_out, subtractor_2_out[2], subtractor_2_out[3]);
  and and_4 (and_4_out, subtractor_2_out[1], subtractor_2_out[3]);
  or or_2 (or_2_out[2], and_1_out, and_2_out, subtractor_1_bout);
  or or_3 (or_3_out[2], and_3_out, and_4_out, subtractor_2_bout);
endmodule
